// Logisim project pipelineMultiplier.circ as structural Verilog: 6 circuits, main circuit main
module main (
  input  [7:0] A1,
  input  [7:0] A2,
  input  [7:0] A3,
  input  [7:0] A4,
  input  [7:0] A5,
  input  [7:0] A6,
  input  [7:0] A7,
  input  [7:0] A8,
  input  [7:0] B1,
  input  [7:0] B2,
  input  [7:0] B3,
  input  [7:0] B4,
  input  [7:0] B5,
  input  [7:0] B6,
  input  [7:0] B7,
  input  [7:0] B8,
  input  Reset,
  output [15:0] SUM,
  output [15:0] AB1,
  output [15:0] AB2,
  output [15:0] AB3,
  output [15:0] AB4,
  output [15:0] AB5,
  output [15:0] AB6,
  output [15:0] AB7,
  output [15:0] AB8
);

  wire Clock_out;
  wire [1:0] Registers__2_bits_3, Registers__2_bits_4;
  wire [2:0] counter_1_q, Registers_2__3_bits_2;
  wire [7:0] adder_1_out, adder_2_out, adder_3_out, adder_4_out, Input_Control_out_18, Input_Control_out_19,
       Input_Control_out_20, Input_Control_out_21, Input_Control_out_22, Input_Control_out_23,
       Input_Control_out_24, Input_Control_out_25;
  wire [7:7] adder_1_cout, adder_3_cout;
  wire [9:0] adder_5_out, adder_6_out, Registers__10_bits_5, Registers__10_bits_6, Registers__10_bits_7,
       Registers__10_bits_8;
  wire [9:9] adder_2_cout, adder_4_cout;
  wire [12:0] adder_7_out, Registers_2__3_bits_3, Registers_2__3_bits_4;

  Clock Clock (.out(Clock_out));
  Counter #(.width(3), .max('h7), .trigger("falling")) counter_1 (
    .Q(counter_1_q), .clk(Clock_out), .clr(Reset));  // open: load, D, count, carry
  Input_Control Input_Control (
    .A1(A1), .A2(A2), .A3(A3), .A4(A4), .A5(A5), .A6(A6), .A7(A7), .A8(A8), .B1(B1), .B2(B2), .B3(B3),
    .B4(B4), .B5(B5), .B6(B6), .B7(B7), .B8(B8), .Counter(counter_1_q), .out_18(Input_Control_out_18),
    .out_19(Input_Control_out_19), .out_20(Input_Control_out_20), .out_21(Input_Control_out_21),
    .out_22(Input_Control_out_22), .out_23(Input_Control_out_23), .out_24(Input_Control_out_24),
    .out_25(Input_Control_out_25));
  Adder adder_1 (
    .a({1'b0, Input_Control_out_18[7:1]}), .b(Input_Control_out_19), .out(adder_1_out), .cout(adder_1_cout[7]));  // open: cin
  Adder adder_2 (
    .a({1'b0, Input_Control_out_20[7:1]}), .b(Input_Control_out_21), .out(adder_2_out), .cout(adder_2_cout[9]));  // open: cin
  Adder adder_3 (
    .a({1'b0, Input_Control_out_22[7:1]}), .b(Input_Control_out_23), .out(adder_3_out), .cout(adder_3_cout[7]));  // open: cin
  Adder adder_4 (
    .a({1'b0, Input_Control_out_24[7:1]}), .b(Input_Control_out_25), .out(adder_4_out), .cout(adder_4_cout[9]));  // open: cin
  regs1 Registers (
    ._2_bits({adder_1_out[0], Input_Control_out_18[0]}),
    ._10_bits({2'b00, adder_1_cout[7], adder_1_out[7:1]}),
    ._10_bits_2({adder_2_cout[9], adder_2_out, Input_Control_out_20[0]}),
    ._2_bits_2({adder_3_out[0], Input_Control_out_22[0]}),
    ._10_bits_3({2'b00, adder_3_cout[7], adder_3_out[7:1]}),
    ._10_bits_4({adder_4_cout[9], adder_4_out, Input_Control_out_24[0]}), .Clock(Clock_out), .Reset(Reset),
    ._2_bits_3(Registers__2_bits_3), ._10_bits_5(Registers__10_bits_5), ._10_bits_6(Registers__10_bits_6),
    ._2_bits_4(Registers__2_bits_4), ._10_bits_7(Registers__10_bits_7), ._10_bits_8(Registers__10_bits_8));
  Adder #(.width(10)) adder_5 (
    .a(Registers__10_bits_5), .b(Registers__10_bits_6), .out(adder_5_out));  // open: cin, cout
  Adder #(.width(10)) adder_6 (
    .a(Registers__10_bits_7), .b(Registers__10_bits_8), .out(adder_6_out));  // open: cin, cout
  regs2 Registers_2 (
    ._3_bits({adder_5_out[0], Registers__2_bits_3}), ._13_bits({4'b0000, adder_5_out[9:1]}),
    ._13_bits_2({adder_6_out, Registers__2_bits_4, 1'b0}), .Clock(Clock_out), .Reset(Reset),
    ._3_bits_2(Registers_2__3_bits_2), ._3_bits_3(Registers_2__3_bits_3), ._3_bits_4(Registers_2__3_bits_4));
  Adder #(.width(13)) adder_7 (
    .a(Registers_2__3_bits_3), .b(Registers_2__3_bits_4), .out(adder_7_out));  // open: cin, cout
  outputControl Output_Control (
    .D({adder_7_out, Registers_2__3_bits_2}), .Counter(counter_1_q), .Clock(Clock_out), .Reset(Reset),
    .out_5(AB1), .out_6(AB2), .out_7(AB3), .out_8(AB4), .out_9(AB5), .out_10(AB6), .out_11(AB7), .out_12(AB8));
  accumulate add_results (
    .in_1(AB1), .in_2(AB2), .in_3(AB3), .in_4(AB4), .in_5(AB5), .in_6(AB6), .in_7(AB7), .in_8(AB8),
    .out_9(SUM));
endmodule

module outputControl (
  input  [15:0] D,
  input  [2:0] Counter,
  input  Clock,
  input  Reset,
  output [15:0] out_5,
  output [15:0] out_6,
  output [15:0] out_7,
  output [15:0] out_8,
  output [15:0] out_9,
  output [15:0] out_10,
  output [15:0] out_11,
  output [15:0] out_12
);

  wire and_1_out, and_2_out, and_3_out, and_4_out, and_5_out, and_6_out, and_7_out, and_8_out,
       decoder_1_out0, decoder_1_out1, decoder_1_out2, decoder_1_out3, decoder_1_out4, decoder_1_out5,
       decoder_1_out6, decoder_1_out7;
  wire [2:0] adder_1_out;

  Decoder #(.select(3), .enable("false")) decoder_1 (
    .out0(decoder_1_out0), .out1(decoder_1_out1), .out2(decoder_1_out2), .out3(decoder_1_out3),
    .out4(decoder_1_out4), .out5(decoder_1_out5), .out6(decoder_1_out6), .out7(decoder_1_out7),
    .sel(adder_1_out));
  Adder #(.width(3)) adder_1 (.a(3'b110), .b(Counter), .out(adder_1_out));  // open: cin, cout
  and and_1 (and_1_out, decoder_1_out0, Clock);
  and and_2 (and_2_out, decoder_1_out1, Clock);
  and and_3 (and_3_out, decoder_1_out2, Clock);
  and and_4 (and_4_out, decoder_1_out3, Clock);
  and and_5 (and_5_out, decoder_1_out4, Clock);
  and and_6 (and_6_out, decoder_1_out5, Clock);
  and and_7 (and_7_out, decoder_1_out6, Clock);
  and and_8 (and_8_out, decoder_1_out7, Clock);
  Register #(.width(16)) register_1 (.D(D), .Q(out_5), .clk(and_1_out), .clr(Reset));  // open: en
  Register #(.width(16)) register_2 (.D(D), .Q(out_6), .clk(and_2_out), .clr(Reset));  // open: en
  Register #(.width(16)) register_3 (.D(D), .Q(out_7), .clk(and_3_out), .clr(Reset));  // open: en
  Register #(.width(16)) register_4 (.D(D), .Q(out_8), .clk(and_4_out), .clr(Reset));  // open: en
  Register #(.width(16)) register_5 (.D(D), .Q(out_9), .clk(and_5_out), .clr(Reset));  // open: en
  Register #(.width(16)) register_6 (.Q(out_10), .clk(and_6_out), .clr(Reset));  // open: D, en
  Register #(.width(16)) register_7 (.D(D), .Q(out_11), .clk(and_7_out), .clr(Reset));  // open: en
  Register #(.width(16)) register_8 (.D(D), .Q(out_12), .clk(and_8_out), .clr(Reset));  // open: en
endmodule

module Input_Control (
  input  [7:0] A1,
  input  [7:0] A2,
  input  [7:0] A3,
  input  [7:0] A4,
  input  [7:0] A5,
  input  [7:0] A6,
  input  [7:0] A7,
  input  [7:0] A8,
  input  [7:0] B1,
  input  [7:0] B2,
  input  [7:0] B3,
  input  [7:0] B4,
  input  [7:0] B5,
  input  [7:0] B6,
  input  [7:0] B7,
  input  [7:0] B8,
  input  [2:0] Counter,
  output [7:0] out_18,
  output [7:0] out_19,
  output [7:0] out_20,
  output [7:0] out_21,
  output [7:0] out_22,
  output [7:0] out_23,
  output [7:0] out_24,
  output [7:0] out_25
);

  wire [7:0] multiplexer_1_out, multiplexer_2_out;

  Multiplexer #(.select(3), .width(8), .enable("false")) multiplexer_1 (
    .in0(A1), .in1(A2), .in2(A3), .in3(A4), .in4(A5), .in5(A6), .in6(A7), .in7(A8), .out(multiplexer_1_out),
    .sel(Counter));
  Multiplexer #(.select(3), .width(8), .enable("false")) multiplexer_2 (
    .in0(B1), .in1(B2), .in2(B3), .in3(B4), .in4(B5), .in5(B6), .in6(B7), .in7(B8), .out(multiplexer_2_out),
    .sel(Counter));
  Multiplexer #(.width(8), .enable("false")) multiplexer_3 (
    .in0({8{1'b0}}), .in1(multiplexer_2_out), .out(out_18), .sel(multiplexer_1_out[0]));
  Multiplexer #(.width(8), .enable("false")) multiplexer_4 (
    .in0({8{1'b0}}), .in1(multiplexer_2_out), .out(out_19), .sel(multiplexer_1_out[1]));
  Multiplexer #(.width(8), .enable("false")) multiplexer_5 (
    .in0({8{1'b0}}), .in1(multiplexer_2_out), .out(out_20), .sel(multiplexer_1_out[2]));
  Multiplexer #(.width(8), .enable("false")) multiplexer_6 (
    .in0({8{1'b0}}), .in1(multiplexer_2_out), .out(out_21), .sel(multiplexer_1_out[3]));
  Multiplexer #(.width(8), .enable("false")) multiplexer_7 (
    .in0({8{1'b0}}), .in1(multiplexer_2_out), .out(out_22), .sel(multiplexer_1_out[4]));
  Multiplexer #(.width(8), .enable("false")) multiplexer_8 (
    .in0({8{1'b0}}), .in1(multiplexer_2_out), .out(out_23), .sel(multiplexer_1_out[5]));
  Multiplexer #(.width(8), .enable("false")) multiplexer_9 (
    .in0({8{1'b0}}), .in1(multiplexer_2_out), .out(out_24), .sel(multiplexer_1_out[6]));
  Multiplexer #(.width(8), .enable("false")) multiplexer_10 (
    .in0({8{1'b0}}), .in1(multiplexer_2_out), .out(out_25), .sel(multiplexer_1_out[7]));
endmodule

module regs1 (
  input  [1:0] _2_bits,
  input  [9:0] _10_bits,
  input  [9:0] _10_bits_2,
  input  [1:0] _2_bits_2,
  input  [9:0] _10_bits_3,
  input  [9:0] _10_bits_4,
  input  Clock,
  input  Reset,
  output [1:0] _2_bits_3,
  output [9:0] _10_bits_5,
  output [9:0] _10_bits_6,
  output [1:0] _2_bits_4,
  output [9:0] _10_bits_7,
  output [9:0] _10_bits_8
);

  Register #(.width(2)) register_1 (.D(_2_bits), .Q(_2_bits_3), .clk(Clock), .clr(Reset));  // open: en
  Register #(.width(10)) register_2 (.D(_10_bits), .Q(_10_bits_5), .clk(Clock), .clr(Reset));  // open: en
  Register #(.width(10)) register_3 (.D(_10_bits_2), .Q(_10_bits_6), .clk(Clock), .clr(Reset));  // open: en
  Register #(.width(2)) register_4 (.D(_2_bits_2), .Q(_2_bits_4), .clk(Clock), .clr(Reset));  // open: en
  Register #(.width(10)) register_5 (.D(_10_bits_3), .Q(_10_bits_7), .clk(Clock), .clr(Reset));  // open: en
  Register #(.width(10)) register_6 (.D(_10_bits_4), .Q(_10_bits_8), .clk(Clock), .clr(Reset));  // open: en
endmodule

module regs2 (
  input  [2:0] _3_bits,
  input  [12:0] _13_bits,
  input  [12:0] _13_bits_2,
  input  Clock,
  input  Reset,
  output [2:0] _3_bits_2,
  output [12:0] _3_bits_3,
  output [12:0] _3_bits_4
);

  Register #(.width(3)) register_1 (.D(_3_bits), .Q(_3_bits_2), .clk(Clock), .clr(Reset));  // open: en
  Register #(.width(13)) register_2 (.D(_13_bits), .Q(_3_bits_3), .clk(Clock), .clr(Reset));  // open: en
  Register #(.width(13)) register_3 (.D(_13_bits_2), .Q(_3_bits_4), .clk(Clock), .clr(Reset));  // open: en
endmodule

module accumulate (
  input  [15:0] in_1,
  input  [15:0] in_2,
  input  [15:0] in_3,
  input  [15:0] in_4,
  input  [15:0] in_5,
  input  [15:0] in_6,
  input  [15:0] in_7,
  input  [15:0] in_8,
  output [15:0] out_9
);

  wire adder_1_cout, adder_2_cout, adder_3_cout, adder_4_cout, adder_5_cout, adder_6_cout;
  wire [15:0] adder_1_out, adder_2_out, adder_3_out, adder_4_out, adder_5_out, adder_6_out;

  Adder #(.width(16)) adder_1 (.a(in_1), .b(in_2), .out(adder_1_out), .cin(adder_5_cout), .cout(adder_1_cout));
  Adder #(.width(16)) adder_2 (.a(in_3), .b(in_4), .out(adder_2_out), .cin(adder_1_cout), .cout(adder_2_cout));
  Adder #(.width(16)) adder_3 (.a(in_5), .b(in_6), .out(adder_3_out), .cin(adder_6_cout), .cout(adder_3_cout));
  Adder #(.width(16)) adder_4 (.a(in_7), .b(in_8), .out(adder_4_out), .cin(adder_3_cout), .cout(adder_4_cout));
  Adder #(.width(16)) adder_5 (
    .a(adder_1_out), .b(adder_2_out), .out(adder_5_out), .cin(adder_2_cout), .cout(adder_5_cout));
  Adder #(.width(16)) adder_6 (
    .a(adder_3_out), .b(adder_4_out), .out(adder_6_out), .cin(adder_4_cout), .cout(adder_6_cout));
  Adder #(.width(16)) adder_7 (.a(adder_5_out), .b(adder_6_out), .out(out_9));  // open: cin, cout
endmodule
